# Fritzing sketch floweronly-shield (saved by Fritzing 0.8.3b)
circuit board: 6.9215cm x 5.33756cm
breadboards: 1

parts:
  Arduino = Arduino
  Bauteil1 = FlowerPad [form="♀ (female)" package=THT]  # not connected
  Bauteil2 = FlowerPad [form="♀ (female)" package=THT]
  Bauteil3 = FlowerPad [form="♀ (female)" package=THT]
  Bauteil4 = FlowerPad [form="♀ (female)" package=THT]
  Bauteil5 = FlowerPad [form="♀ (female)" package=THT]
  Bauteil6 = FlowerPad [form="♀ (female)" package=THT]
  Bauteil7 = FlowerPad [form="♀ (female)" package=THT]
  Bauteil8 = FlowerPad [form="♀ (female)" package=THT]  # not connected
  Bauteil9 = FlowerPad [form="♀ (female)" package=THT]
  Bauteil10 = FlowerPad [form="♀ (female)" package=THT]  # not connected
  Bauteil11 = FlowerPad [form="♀ (female)" package=THT]
  Bauteil12 = FlowerPad [form="♀ (female)" package=THT]  # not connected
  Bauteil13 = FlowerPad [form="♀ (female)" package=THT]
  Bauteil14 = FlowerPad [form="♀ (female)" package=THT]  # not connected
  Bauteil15 = FlowerPad [form="♀ (female)" package=THT]
  Bauteil16 = FlowerPad [form="♀ (female)" package=THT]  # not connected
  Bauteil17 = FlowerPad [form="♀ (female)" package=THT]
  Bauteil18 = FlowerPad [form="♀ (female)" package=THT]  # not connected
  Bauteil19 = FlowerPad [form="♀ (female)" package=THT]  # not connected
  Bauteil20 = FlowerPad [form="♀ (female)" package=THT]  # not connected
  Bauteil21 = FlowerPad [form="♀ (female)" package=THT]
  Bauteil22 = FlowerPad [form="♀ (female)" package=THT]
  Bauteil24 = FlowerPad [form="♀ (female)" package=THT]  # not connected
  Bauteil25 = FlowerPad [form="♀ (female)" package=THT]  # not connected
  Bauteil26 = FlowerPad [form="♀ (female)" package=THT]  # not connected
  Bauteil27 = FlowerPad [form="♀ (female)" package=THT]  # not connected
  Bauteil28 = FlowerPad [form="♀ (female)" package=THT]  # not connected
  Bauteil29 = FlowerPad [form="♀ (female)" package=THT]
  Bauteil30 = FlowerPad [form="♀ (female)" package=THT]  # not connected
  Bauteil31 = FlowerPad [form="♀ (female)" package=THT]  # not connected
  Bauteil32 = FlowerPad [form="♀ (female)" package=THT]  # not connected
  Bauteil33 = FlowerPad [form="♀ (female)" package=THT]  # not connected
  Bauteil34 = FlowerPad [form="♀ (female)" package=THT]  # not connected
  Bauteil35 = FlowerPad [form="♀ (female)" package=THT]  # not connected
  Bauteil36 = FlowerPad [form="♀ (female)" package=THT]  # not connected
  Bauteil37 = FlowerPad [form="♀ (female)" package=THT]  # not connected
  Bauteil38 = FlowerPad [form="♀ (female)" package=THT]  # not connected
  Bauteil39 = FlowerPad [form="♀ (female)" package=THT]  # not connected
  Bauteil40 = FlowerPad [form="♀ (female)" package=THT]  # not connected
  Bauteil42 = FlowerPad [form="♀ (female)" package=THT]  # not connected
  Bauteil44 = FlowerPad [form="♀ (female)" package=THT]  # not connected
  Bauteil45 = FlowerPad [form="♀ (female)" package=THT]
  Bauteil46 = FlowerPad [form="♀ (female)" package=THT]
  Bauteil47 = FlowerPad [form="♀ (female)" package=THT]
  Bauteil48 = FlowerPad [form="♀ (female)" package=THT]
  Bauteil49 = FlowerPad [form="♀ (female)" package=THT]
  Bauteil50 = FlowerPad [form="♀ (female)" package=THT]
  Bauteil51 = FlowerPad [form="♀ (female)" package=THT]
  Bauteil52 = FlowerPad [form="♀ (female)" package=THT]
  Bauteil53 = FlowerPad [form="♀ (female)" package=THT]
  Bauteil54 = FlowerPad [form="♀ (female)" package=THT]
  Bauteil55 = FlowerPad [form="♀ (female)" package=THT]
  Bauteil56 = FlowerPad [form="♀ (female)" package=THT]
  Bauteil57 = FlowerPad [form="♀ (female)" package=THT]
  Bauteil58 = FlowerPad [form="♀ (female)" package=THT]
  Bauteil59 = FlowerPad [form="♀ (female)" package=THT]
  Bauteil60 = FlowerPad [form="♀ (female)" package=THT]
  Bauteil62 = FlowerPad [form="♀ (female)" package=THT]
  Bauteil63 = FlowerPad [form="♀ (female)" package=THT]
  Bauteil64 = FlowerPad [form="♀ (female)" package=THT]
  Bauteil65 = FlowerPad [form="♀ (female)" package=THT]
  Bauteil66 = FlowerPad [form="♀ (female)" package=THT]
  Bauteil67 = FlowerPad [form="♀ (female)" package=THT]
  Bauteil68 = FlowerPad [form="♀ (female)" package=THT]
  Bauteil69 = FlowerPad [form="♀ (female)" package=THT]
  Bauteil70 = FlowerPad [form="♀ (female)" package=THT]  # not connected
  Bauteil91 = FlowerPad [form="♀ (female)" package=THT]
  Bauteil92 = FlowerPad [form="♀ (female)" package=THT]
  Bauteil93 = FlowerPad [form="♀ (female)" package=THT]
  Bauteil94 = FlowerPad [form="♀ (female)" package=THT]
  Bauteil95 = FlowerPad [form="♀ (female)" package=THT]  # not connected
  Bauteil96 = FlowerPad [form="♀ (female)" package=THT]  # not connected
  Bauteil97 = FlowerPad [form="♀ (female)" package=THT]  # not connected
  Bauteil98 = FlowerPad [form="♀ (female)" package=THT]  # not connected
  Bauteil101 = FlowerPad [form="♀ (female)" package=THT]  # not connected
  Bauteil102 = FlowerPad [form="♀ (female)" package=THT]  # not connected
  Bauteil104 = FlowerPad [form="♀ (female)" package=THT]  # not connected
  Bauteil105 = FlowerPad [form="♀ (female)" package=THT]  # not connected
  Bauteil106 = FlowerPad [form="♀ (female)" package=THT]  # not connected
  Bauteil107 = FlowerPad [form="♀ (female)" package=THT]  # not connected
  Bauteil108 = FlowerPad [form="♀ (female)" package=THT]  # not connected
  Bauteil109 = FlowerPad [form="♀ (female)" package=THT]  # not connected
  Bauteil110 = FlowerPad [form="♀ (female)" package=THT]  # not connected
  Bauteil111 = FlowerPad [form="♀ (female)" package=THT]  # not connected
  Bauteil112 = FlowerPad [form="♀ (female)" package=THT]  # not connected
  Bauteil113 = FlowerPad [form="♀ (female)" package=THT]
  Bauteil114 = FlowerPad [form="♀ (female)" package=THT]
  Bauteil115 = FlowerPad [form="♀ (female)" package=THT]
  Bauteil116 = FlowerPad [form="♀ (female)" package=THT]
  Bauteil117 = FlowerPad [form="♀ (female)" package=THT]
  Bauteil120 = FlowerPad [form="♀ (female)" package=THT]
  Bauteil121 = FlowerPad [form="♀ (female)" package=THT]
  Bauteil122 = FlowerPad [form="♀ (female)" package=THT]
  Bauteil123 = FlowerPad [form="♀ (female)" package=THT]
  Bauteil124 = FlowerPad [form="♀ (female)" package=THT]
  Bauteil144 = FlowerPad [form="♀ (female)" package=THT]
  Bauteil145 = FlowerPad [form="♀ (female)" package=THT]  # not connected
  Bauteil146 = FlowerPad [form="♀ (female)" package=THT]  # not connected
  Bauteil147 = FlowerPad [form="♀ (female)" package=THT]  # not connected
  Bauteil148 = FlowerPad [form="♀ (female)" package=THT]  # not connected
  Bauteil149 = FlowerPad [form="♀ (female)" package=THT]  # not connected
  Bauteil150 = FlowerPad [form="♀ (female)" package=THT]  # not connected
  Bauteil151 = FlowerPad [form="♀ (female)" package=THT]  # not connected
  Bauteil152 = FlowerPad [form="♀ (female)" package=THT]  # not connected
  Bauteil153 = FlowerPad [form="♀ (female)" package=THT]  # not connected
  Bauteil154 = FlowerPad [form="♀ (female)" package=THT]  # not connected
  Bauteil155 = FlowerPad [form="♀ (female)" package=THT]  # not connected
  Bauteil156 = FlowerPad [form="♀ (female)" package=THT]  # not connected
  Bauteil157 = FlowerPad [form="♀ (female)" package=THT]  # not connected
  Bauteil158 = FlowerPad [form="♀ (female)" package=THT]  # not connected
  Bauteil159 = FlowerPad [form="♀ (female)" package=THT]  # not connected
  Bauteil160 = FlowerPad [form="♀ (female)" package=THT]  # not connected
  Bauteil161 = FlowerPad [form="♀ (female)" package=THT]  # not connected
  Bauteil162 = FlowerPad [form="♀ (female)" package=THT]  # not connected
  Bauteil163 = FlowerPad [form="♀ (female)" package=THT]  # not connected
  Bauteil164 = FlowerPad [form="♀ (female)" package=THT]  # not connected
  Bauteil165 = FlowerPad [form="♀ (female)" package=THT]  # not connected
  Bauteil166 = FlowerPad [form="♀ (female)" package=THT]  # not connected
  Bauteil167 = FlowerPad [form="♀ (female)" package=THT]  # not connected
  Bauteil168 = FlowerPad [form="♀ (female)" package=THT]  # not connected
  Bauteil169 = FlowerPad [form="♀ (female)" package=THT]  # not connected
  Bauteil170 = FlowerPad [form="♀ (female)" package=THT]  # not connected
  Bauteil171 = FlowerPad [form="♀ (female)" package=THT]  # not connected
  Bauteil172 = FlowerPad [form="♀ (female)" package=THT]  # not connected
  Bauteil173 = FlowerPad [form="♀ (female)" package=THT]  # not connected
  Bauteil174 = FlowerPad [form="♀ (female)" package=THT]  # not connected
  Bauteil175 = FlowerPad [form="♀ (female)" package=THT]  # not connected
  Bauteil176 = FlowerPad [form="♀ (female)" package=THT]  # not connected
  Bauteil177 = FlowerPad [form="♀ (female)" package=THT]  # not connected
  Bauteil178 = FlowerPad [form="♀ (female)" package=THT]  # not connected
  Bauteil180 = FlowerPad [form="♀ (female)" package=THT]  # not connected
  Bauteil181 = FlowerPad [form="♀ (female)" package=THT]  # not connected
  Bauteil182 = FlowerPad [form="♀ (female)" package=THT]  # not connected
  Bauteil183 = FlowerPad [form="♀ (female)" package=THT]  # not connected
  Bauteil184 = FlowerPad [form="♀ (female)" package=THT]  # not connected
  Bauteil185 = FlowerPad [form="♀ (female)" package=THT]  # not connected
  Bauteil186 = FlowerPad [form="♀ (female)" package=THT]  # not connected
  Bauteil187 = FlowerPad [form="♀ (female)" package=THT]  # not connected
  Bauteil188 = FlowerPad [form="♀ (female)" package=THT]  # not connected
  Bauteil190 = FlowerPad [form="♀ (female)" package=THT]  # not connected
  Bauteil191 = FlowerPad [form="♀ (female)" package=THT]  # not connected
  Bauteil192 = FlowerPad [form="♀ (female)" package=THT]  # not connected
  Bauteil193 = FlowerPad [form="♀ (female)" package=THT]  # not connected
  Bauteil194 = FlowerPad [form="♀ (female)" package=THT]  # not connected
  Bauteil195 = FlowerPad [form="♀ (female)" package=THT]  # not connected
  Bauteil196 = FlowerPad [form="♀ (female)" package=THT]  # not connected
  Bauteil197 = FlowerPad [form="♀ (female)" package=THT]  # not connected
  Bauteil198 = FlowerPad [form="♀ (female)" package=THT]  # not connected
  Bauteil199 = FlowerPad [form="♀ (female)" package=THT]  # not connected
  Bauteil200 = FlowerPad [form="♀ (female)" package=THT]  # not connected
  Bauteil201 = FlowerPad [form="♀ (female)" package=THT]  # not connected
  Bauteil202 = FlowerPad [form="♀ (female)" package=THT]  # not connected
  Bauteil203 = FlowerPad [form="♀ (female)" package=THT]  # not connected
  Bauteil205 = FlowerPad [form="♀ (female)" package=THT]  # not connected
  Bauteil206 = FlowerPad [form="♀ (female)" package=THT]  # not connected
  Bauteil207 = FlowerPad [form="♀ (female)" package=THT]  # not connected
  Bauteil208 = FlowerPad [form="♀ (female)" package=THT]  # not connected
  Bauteil209 = FlowerPad [form="♀ (female)" package=THT]  # not connected
  Bauteil210 = FlowerPad [form="♀ (female)" package=THT]  # not connected
  Bauteil211 = FlowerPad [form="♀ (female)" package=THT]  # not connected
  Bauteil212 = FlowerPad [form="♀ (female)" package=THT]  # not connected
  Bauteil213 = FlowerPad [form="♀ (female)" package=THT]  # not connected
  Bauteil214 = FlowerPad [form="♀ (female)" package=THT]  # not connected
  Bauteil215 = FlowerPad [form="♀ (female)" package=THT]  # not connected
  Bauteil216 = FlowerPad [form="♀ (female)" package=THT]  # not connected
  Bauteil217 = FlowerPad [form="♀ (female)" package=THT]  # not connected
  Bauteil218 = FlowerPad [form="♀ (female)" package=THT]  # not connected
  Bauteil219 = FlowerPad [form="♀ (female)" package=THT]  # not connected
  Bauteil221 = FlowerPad [form="♀ (female)" package=THT]  # not connected
  Bauteil222 = FlowerPad [form="♀ (female)" package=THT]  # not connected
  Bauteil239 = FlowerPad [form="♀ (female)" package=THT]  # not connected
  Bauteil240 = FlowerPad [form="♀ (female)" package=THT]  # not connected
  Bauteil241 = FlowerPad [form="♀ (female)" package=THT]  # not connected
  Bauteil242 = FlowerPad [form="♀ (female)" package=THT]  # not connected
  Bauteil243 = FlowerPad [form="♀ (female)" package=THT]  # not connected
  Bauteil244 = FlowerPad [form="♀ (female)" package=THT]  # not connected
  Bauteil245 = FlowerPad [form="♀ (female)" package=THT]  # not connected
  Bauteil246 = FlowerPad [form="♀ (female)" package=THT]  # not connected
  Bauteil247 = FlowerPad [form="♀ (female)" package=THT]  # not connected
  Bauteil248 = FlowerPad [form="♀ (female)" package=THT]  # not connected
  Bauteil249 = FlowerPad [form="♀ (female)" package=THT]  # not connected
  Bauteil250 = FlowerPad [form="♀ (female)" package=THT]  # not connected
  Bauteil251 = FlowerPad [form="♀ (female)" package=THT]  # not connected
  Bauteil252 = FlowerPad [form="♀ (female)" package=THT]  # not connected
  Bauteil253 = FlowerPad [form="♀ (female)" package=THT]  # not connected
  Bauteil254 = FlowerPad [form="♀ (female)" package=THT]  # not connected
  Bauteil255 = FlowerPad [form="♀ (female)" package=THT]  # not connected
  Bauteil256 = FlowerPad [form="♀ (female)" package=THT]  # not connected
  Bauteil257 = FlowerPad [form="♀ (female)" package=THT]  # not connected
  Bauteil258 = FlowerPad [form="♀ (female)" package=THT]  # not connected
  Bauteil259 = FlowerPad [form="♀ (female)" package=THT]  # not connected
  Bauteil260 = FlowerPad [form="♀ (female)" package=THT]  # not connected
  Bauteil261 = FlowerPad [form="♀ (female)" package=THT]  # not connected
  Bauteil262 = FlowerPad [form="♀ (female)" package=THT]  # not connected
  Bauteil263 = FlowerPad [form="♀ (female)" package=THT]  # not connected
  Bauteil264 = FlowerPad [form="♀ (female)" package=THT]  # not connected
  Bauteil265 = FlowerPad [form="♀ (female)" package=THT]  # not connected
  Bauteil266 = FlowerPad [form="♀ (female)" package=THT]  # not connected
  Bauteil267 = FlowerPad [form="♀ (female)" package=THT]  # not connected
  Bauteil268 = FlowerPad [form="♀ (female)" package=THT]  # not connected
  Bauteil269 = FlowerPad [form="♀ (female)" package=THT]  # not connected
  Bauteil270 = FlowerPad [form="♀ (female)" package=THT]  # not connected
  Bauteil271 = FlowerPad [form="♀ (female)" package=THT]  # not connected
  Bauteil272 = FlowerPad [form="♀ (female)" package=THT]  # not connected
  Bauteil273 = FlowerPad [form="♀ (female)" package=THT]  # not connected
  Bauteil274 = FlowerPad [form="♀ (female)" package=THT]  # not connected
  Bauteil275 = FlowerPad [form="♀ (female)" package=THT]  # not connected
  Bauteil276 = FlowerPad [form="♀ (female)" package=THT]  # not connected
  Bauteil277 = FlowerPad [form="♀ (female)" package=THT]  # not connected
  Bauteil278 = FlowerPad [form="♀ (female)" package=THT]  # not connected
  Bauteil279 = FlowerPad [form="♀ (female)" package=THT]  # not connected
  Bauteil280 = FlowerPad [form="♀ (female)" package=THT]  # not connected
  Bauteil281 = FlowerPad [form="♀ (female)" package=THT]  # not connected
  Bauteil282 = FlowerPad [form="♀ (female)" package=THT]  # not connected
  Bauteil283 = FlowerPad [form="♀ (female)" package=THT]  # not connected
  Bauteil284 = FlowerPad [form="♀ (female)" package=THT]  # not connected
  Bauteil285 = FlowerPad [form="♀ (female)" package=THT]  # not connected
  Bauteil286 = FlowerPad [form="♀ (female)" package=THT]  # not connected
  Bauteil287 = FlowerPad [form="♀ (female)" package=THT]  # not connected
  Bauteil288 = FlowerPad [form="♀ (female)" package=THT]  # not connected
  Bauteil289 = FlowerPad [form="♀ (female)" package=THT]  # not connected
  Bauteil290 = FlowerPad [form="♀ (female)" package=THT]  # not connected
  Bauteil291 = FlowerPad [form="♀ (female)" package=THT]  # not connected
  Bauteil292 = FlowerPad [form="♀ (female)" package=THT]  # not connected
  Bauteil293 = FlowerPad [form="♀ (female)" package=THT]  # not connected
  Bauteil294 = FlowerPad [form="♀ (female)" package=THT]  # not connected
  Bauteil295 = FlowerPad [form="♀ (female)" package=THT]  # not connected
  Bauteil296 = FlowerPad [form="♀ (female)" package=THT]  # not connected
  Bauteil297 = FlowerPad [form="♀ (female)" package=THT]  # not connected
  Bauteil298 = FlowerPad [form="♀ (female)" package=THT]  # not connected
  Bauteil299 = FlowerPad [form="♀ (female)" package=THT]  # not connected
  Bauteil300 = FlowerPad [form="♀ (female)" package=THT]
  Bauteil301 = FlowerPad [form="♀ (female)" package=THT]  # not connected
  Bauteil302 = FlowerPad [form="♀ (female)" package=THT]
  Bauteil303 = FlowerPad [form="♀ (female)" package=THT]
  Bauteil304 = FlowerPad [form="♀ (female)" package=THT]  # not connected
  Bauteil305 = FlowerPad [form="♀ (female)" package=THT]
  Bauteil306 = FlowerPad [form="♀ (female)" package=THT]
  Bauteil307 = FlowerPad [form="♀ (female)" package=THT]
  Bauteil308 = FlowerPad [form="♀ (female)" package=THT]
  Bauteil309 = FlowerPad [form="♀ (female)" package=THT]  # not connected
  Bauteil310 = FlowerPad [form="♀ (female)" package=THT]  # not connected
  Bauteil311 = FlowerPad [form="♀ (female)" package=THT]  # not connected
  Bauteil312 = FlowerPad [form="♀ (female)" package=THT]  # not connected
  Bauteil313 = FlowerPad [form="♀ (female)" package=THT]  # not connected
  Bauteil464 = FlowerPad [form="♀ (female)" package=THT]  # not connected
  Bauteil465 = FlowerPad [form="♀ (female)" package=THT]  # not connected
  Bauteil466 = FlowerPad [form="♀ (female)" package=THT]  # not connected
  Bauteil467 = FlowerPad [form="♀ (female)" package=THT]  # not connected
  Bauteil468 = FlowerPad [form="♀ (female)" package=THT]  # not connected
  Bauteil469 = FlowerPad [form="♀ (female)" package=THT]  # not connected
  Bauteil470 = FlowerPad [form="♀ (female)" package=THT]  # not connected
  Bauteil471 = FlowerPad [form="♀ (female)" package=THT]  # not connected
  Bauteil472 = FlowerPad [form="♀ (female)" package=THT]  # not connected
  Bauteil473 = FlowerPad [form="♀ (female)" package=THT]  # not connected
  Bauteil474 = FlowerPad [form="♀ (female)" package=THT]  # not connected
  Bauteil475 = FlowerPad [form="♀ (female)" package=THT]  # not connected
  Bauteil476 = FlowerPad [form="♀ (female)" package=THT]  # not connected
  Bauteil477 = FlowerPad [form="♀ (female)" package=THT]  # not connected
  Bauteil478 = FlowerPad [form="♀ (female)" package=THT]  # not connected
  Bauteil479 = FlowerPad [form="♀ (female)" package=THT]  # not connected
  Bauteil480 = FlowerPad [form="♀ (female)" package=THT]  # not connected
  Bauteil481 = FlowerPad [form="♀ (female)" package=THT]  # not connected
  Bauteil482 = FlowerPad [form="♀ (female)" package=THT]  # not connected
  Bauteil483 = FlowerPad [form="♀ (female)" package=THT]  # not connected
  Bauteil484 = FlowerPad [form="♀ (female)" package=THT]  # not connected
  Bauteil485 = FlowerPad [form="♀ (female)" package=THT]  # not connected
  Bauteil486 = FlowerPad [form="♀ (female)" package=THT]  # not connected
  Bauteil487 = FlowerPad [form="♀ (female)" package=THT]  # not connected
  Bauteil488 = FlowerPad [form="♀ (female)" package=THT]  # not connected
  Bauteil489 = FlowerPad [form="♀ (female)" package=THT]  # not connected
  Bauteil490 = FlowerPad [form="♀ (female)" package=THT]  # not connected
  Bauteil491 = FlowerPad [form="♀ (female)" package=THT]  # not connected
  Bauteil492 = FlowerPad [form="♀ (female)" package=THT]  # not connected
  Bauteil493 = FlowerPad [form="♀ (female)" package=THT]  # not connected
  Bauteil494 = FlowerPad [form="♀ (female)" package=THT]  # not connected
  Bauteil495 = FlowerPad [form="♀ (female)" package=THT]  # not connected
  Bauteil496 = FlowerPad [form="♀ (female)" package=THT]  # not connected
  Bauteil497 = FlowerPad [form="♀ (female)" package=THT]  # not connected
  Bauteil498 = FlowerPad [form="♀ (female)" package=THT]  # not connected
  Bauteil499 = FlowerPad [form="♀ (female)" package=THT]  # not connected
  Bauteil500 = FlowerPad [form="♀ (female)" package=THT]  # not connected
  Bauteil501 = FlowerPad [form="♀ (female)" package=THT]  # not connected
  Bauteil502 = FlowerPad [form="♀ (female)" package=THT]  # not connected
  Bauteil503 = FlowerPad [form="♀ (female)" package=THT]  # not connected
  Bauteil504 = FlowerPad [form="♀ (female)" package=THT]  # not connected
  Bauteil505 = FlowerPad [form="♀ (female)" package=THT]  # not connected
  Bauteil506 = FlowerPad [form="♀ (female)" package=THT]  # not connected
  Bauteil507 = FlowerPad [form="♀ (female)" package=THT]  # not connected
  Bauteil508 = FlowerPad [form="♀ (female)" package=THT]  # not connected
  Bauteil509 = FlowerPad [form="♀ (female)" package=THT]  # not connected
  Bauteil510 = FlowerPad [form="♀ (female)" package=THT]  # not connected
  Bauteil511 = FlowerPad [form="♀ (female)" package=THT]  # not connected
  Bauteil512 = FlowerPad [form="♀ (female)" package=THT]  # not connected
  Bauteil513 = FlowerPad [form="♀ (female)" package=THT]  # not connected
  Bauteil514 = FlowerPad [form="♀ (female)" package=THT]  # not connected
  Bauteil515 = FlowerPad [form="♀ (female)" package=THT]  # not connected
  Bauteil516 = FlowerPad [form="♀ (female)" package=THT]  # not connected
  Bauteil517 = FlowerPad [form="♀ (female)" package=THT]  # not connected
  Bauteil518 = FlowerPad [form="♀ (female)" package=THT]  # not connected
  Bauteil519 = FlowerPad [form="♀ (female)" package=THT]  # not connected
  Bauteil520 = FlowerPad [form="♀ (female)" package=THT]  # not connected
  Bauteil521 = FlowerPad [form="♀ (female)" package=THT]  # not connected
  Bauteil522 = FlowerPad [form="♀ (female)" package=THT]  # not connected
  Bauteil523 = FlowerPad [form="♀ (female)" package=THT]  # not connected
  Bauteil524 = FlowerPad [form="♀ (female)" package=THT]  # not connected
  Bauteil525 = FlowerPad [form="♀ (female)" package=THT]  # not connected
  Bauteil526 = FlowerPad [form="♀ (female)" package=THT]  # not connected
  Bauteil527 = FlowerPad [form="♀ (female)" package=THT]  # not connected
  Bauteil528 = FlowerPad [form="♀ (female)" package=THT]  # not connected
  Bauteil529 = FlowerPad [form="♀ (female)" package=THT]  # not connected
  Bauteil530 = FlowerPad [form="♀ (female)" package=THT]  # not connected
  Bauteil531 = FlowerPad [form="♀ (female)" package=THT]  # not connected
  Bauteil532 = FlowerPad [form="♀ (female)" package=THT]  # not connected
  Bauteil533 = FlowerPad [form="♀ (female)" package=THT]  # not connected
  Bauteil534 = FlowerPad [form="♀ (female)" package=THT]  # not connected
  Bauteil535 = FlowerPad [form="♀ (female)" package=THT]  # not connected
  Bauteil536 = FlowerPad [form="♀ (female)" package=THT]  # not connected
  Bauteil537 = FlowerPad [form="♀ (female)" package=THT]  # not connected
  Bauteil538 = FlowerPad [form="♀ (female)" package=THT]  # not connected
  Bauteil539 = FlowerPad [form="♀ (female)" package=THT]  # not connected
  Bauteil540 = FlowerPad [form="♀ (female)" package=THT]  # not connected
  Bauteil541 = FlowerPad [form="♀ (female)" package=THT]  # not connected
  Bauteil542 = FlowerPad [form="♀ (female)" package=THT]  # not connected
  Bauteil543 = FlowerPad [form="♀ (female)" package=THT]  # not connected
  Bauteil544 = FlowerPad [form="♀ (female)" package=THT]  # not connected
  Bauteil545 = FlowerPad [form="♀ (female)" package=THT]  # not connected
  Bauteil546 = FlowerPad [form="♀ (female)" package=THT]  # not connected
  Bauteil547 = FlowerPad [form="♀ (female)" package=THT]  # not connected
  Bauteil548 = FlowerPad [form="♀ (female)" package=THT]  # not connected
  Bauteil549 = FlowerPad [form="♀ (female)" package=THT]  # not connected
  Bauteil550 = FlowerPad [form="♀ (female)" package=THT]  # not connected
  Bauteil551 = FlowerPad [form="♀ (female)" package=THT]  # not connected
  Bauteil552 = FlowerPad [form="♀ (female)" package=THT]  # not connected
  Bauteil553 = FlowerPad [form="♀ (female)" package=THT]  # not connected
  Bauteil554 = FlowerPad [form="♀ (female)" package=THT]  # not connected
  Bauteil555 = FlowerPad [form="♀ (female)" package=THT]  # not connected
  Bauteil556 = FlowerPad [form="♀ (female)" package=THT]  # not connected
  Bauteil557 = FlowerPad [form="♀ (female)" package=THT]  # not connected
  Bauteil558 = FlowerPad [form="♀ (female)" package=THT]  # not connected
  Bauteil559 = FlowerPad [form="♀ (female)" package=THT]  # not connected
  Bauteil560 = FlowerPad [form="♀ (female)" package=THT]  # not connected
  Bauteil561 = FlowerPad [form="♀ (female)" package=THT]  # not connected
  Bauteil562 = FlowerPad [form="♀ (female)" package=THT]  # not connected
  Bauteil563 = FlowerPad [form="♀ (female)" package=THT]  # not connected
  Bauteil564 = FlowerPad [form="♀ (female)" package=THT]  # not connected
  Bauteil565 = FlowerPad [form="♀ (female)" package=THT]  # not connected
  Bauteil566 = FlowerPad [form="♀ (female)" package=THT]  # not connected
  Bauteil567 = FlowerPad [form="♀ (female)" package=THT]  # not connected
  Bauteil568 = FlowerPad [form="♀ (female)" package=THT]  # not connected
  Bauteil569 = FlowerPad [form="♀ (female)" package=THT]  # not connected
  Bauteil570 = FlowerPad [form="♀ (female)" package=THT]  # not connected
  Bauteil571 = FlowerPad [form="♀ (female)" package=THT]  # not connected
  Bauteil572 = FlowerPad [form="♀ (female)" package=THT]  # not connected
  Bauteil573 = FlowerPad [form="♀ (female)" package=THT]  # not connected
  Bauteil574 = FlowerPad [form="♀ (female)" package=THT]  # not connected
  Bauteil575 = FlowerPad [form="♀ (female)" package=THT]  # not connected
  Bauteil576 = FlowerPad [form="♀ (female)" package=THT]  # not connected
  Bauteil577 = FlowerPad [form="♀ (female)" package=THT]  # not connected
  Bauteil578 = FlowerPad [form="♀ (female)" package=THT]  # not connected
  Bauteil579 = FlowerPad [form="♀ (female)" package=THT]  # not connected
  Bauteil580 = FlowerPad [form="♀ (female)" package=THT]  # not connected
  Bauteil581 = FlowerPad [form="♀ (female)" package=THT]  # not connected
  Bauteil582 = FlowerPad [form="♀ (female)" package=THT]  # not connected
  Bauteil583 = FlowerPad [form="♀ (female)" package=THT]  # not connected
  Bauteil584 = FlowerPad [form="♀ (female)" package=THT]  # not connected
  Bauteil585 = FlowerPad [form="♀ (female)" package=THT]  # not connected
  Bauteil586 = FlowerPad [form="♀ (female)" package=THT]  # not connected
  Bauteil587 = FlowerPad [form="♀ (female)" package=THT]  # not connected
  Bauteil588 = FlowerPad [form="♀ (female)" package=THT]  # not connected
  Bauteil589 = FlowerPad [form="♀ (female)" package=THT]  # not connected
  Bauteil590 = FlowerPad [form="♀ (female)" package=THT]  # not connected
  Bauteil591 = FlowerPad [form="♀ (female)" package=THT]  # not connected
  Bauteil592 = FlowerPad [form="♀ (female)" package=THT]  # not connected
  Bauteil593 = FlowerPad [form="♀ (female)" package=THT]  # not connected
  Bauteil594 = FlowerPad [form="♀ (female)" package=THT]  # not connected
  Bauteil595 = FlowerPad [form="♀ (female)" package=THT]  # not connected
  Bauteil596 = FlowerPad [form="♀ (female)" package=THT]  # not connected
  Bauteil597 = FlowerPad [form="♀ (female)" package=THT]  # not connected
  Bauteil598 = FlowerPad [form="♀ (female)" package=THT]  # not connected
  Bauteil599 = FlowerPad [form="♀ (female)" package=THT]  # not connected
  Bauteil600 = FlowerPad [form="♀ (female)" package=THT]  # not connected
  Bauteil601 = FlowerPad [form="♀ (female)" package=THT]  # not connected
  Bauteil602 = FlowerPad [form="♀ (female)" package=THT]  # not connected
  Bauteil603 = FlowerPad [form="♀ (female)" package=THT]  # not connected
  Bauteil604 = FlowerPad [form="♀ (female)" package=THT]  # not connected
  Bauteil605 = FlowerPad [form="♀ (female)" package=THT]  # not connected
  Bauteil606 = FlowerPad [form="♀ (female)" package=THT]  # not connected
  Bauteil607 = FlowerPad [form="♀ (female)" package=THT]  # not connected
  Bauteil608 = FlowerPad [form="♀ (female)" package=THT]  # not connected
  Bauteil609 = FlowerPad [form="♀ (female)" package=THT]  # not connected
  Bauteil610 = FlowerPad [form="♀ (female)" package=THT]  # not connected
  Bauteil611 = FlowerPad [form="♀ (female)" package=THT]  # not connected
  Bauteil612 = FlowerPad [form="♀ (female)" package=THT]  # not connected
  Bauteil613 = FlowerPad [form="♀ (female)" package=THT]  # not connected
  Bauteil614 = FlowerPad [form="♀ (female)" package=THT]  # not connected
  Bauteil615 = FlowerPad [form="♀ (female)" package=THT]  # not connected
  Bauteil616 = FlowerPad [form="♀ (female)" package=THT]  # not connected
  Bauteil617 = FlowerPad [form="♀ (female)" package=THT]  # not connected
  Bauteil618 = FlowerPad [form="♀ (female)" package=THT]  # not connected
  Bauteil619 = FlowerPad [form="♀ (female)" package=THT]  # not connected
  Bauteil620 = FlowerPad [form="♀ (female)" package=THT]  # not connected
  Bauteil621 = FlowerPad [form="♀ (female)" package=THT]  # not connected
  Bauteil622 = FlowerPad [form="♀ (female)" package=THT]  # not connected
  Bauteil623 = FlowerPad [form="♀ (female)" package=THT]  # not connected
  Bauteil624 = FlowerPad [form="♀ (female)" package=THT]  # not connected
  Bauteil625 = FlowerPad [form="♀ (female)" package=THT]  # not connected
  Bauteil626 = FlowerPad [form="♀ (female)" package=THT]  # not connected
  Bauteil627 = FlowerPad [form="♀ (female)" package=THT]  # not connected
  Bauteil628 = FlowerPad [form="♀ (female)" package=THT]  # not connected
  Bauteil629 = FlowerPad [form="♀ (female)" package=THT]  # not connected
  Bauteil630 = FlowerPad [form="♀ (female)" package=THT]  # not connected
  Bauteil631 = FlowerPad [form="♀ (female)" package=THT]  # not connected
  Bauteil632 = FlowerPad [form="♀ (female)" package=THT]  # not connected
  Bauteil633 = FlowerPad [form="♀ (female)" package=THT]  # not connected
  Bauteil634 = FlowerPad [form="♀ (female)" package=THT]  # not connected
  Bauteil635 = FlowerPad [form="♀ (female)" package=THT]  # not connected
  Bauteil636 = FlowerPad [form="♀ (female)" package=THT]  # not connected
  Bauteil637 = FlowerPad [form="♀ (female)" package=THT]  # not connected
  Bauteil638 = FlowerPad [form="♀ (female)" package=THT]  # not connected
  Bauteil639 = FlowerPad [form="♀ (female)" package=THT]  # not connected
  Bauteil640 = FlowerPad [form="♀ (female)" package=THT]  # not connected
  Bauteil641 = FlowerPad [form="♀ (female)" package=THT]  # not connected
  Bauteil642 = FlowerPad [form="♀ (female)" package=THT]  # not connected
  Bauteil643 = FlowerPad [form="♀ (female)" package=THT]  # not connected

nets:
  N1: Arduino.aref, Bauteil53.pin1
  N2: Arduino.GND, Bauteil21.pin1, Bauteil22.pin1, Bauteil55.pin1, Bauteil116.pin1, Bauteil117.pin1, Bauteil144.pin1, Bauteil300.pin1, Bauteil302.pin1, Bauteil303.pin1, Bauteil305.pin1, Bauteil306.pin1, Bauteil307.pin1, Bauteil308.pin1
  N3: Arduino.D13, Bauteil56.pin1
  N4: Arduino.D12, Bauteil54.pin1
  N5: Arduino.D11, Bauteil58.pin1
  N6: Arduino.D10, Bauteil59.pin1
  N7: Arduino.D9, Bauteil57.pin1
  N8: Arduino.D8, Bauteil60.pin1
  N9: Arduino.D7, Bauteil62.pin1
  N10: Arduino.D6, Bauteil64.pin1
  N11: Arduino.D5, Bauteil65.pin1
  N12: Arduino.D4, Bauteil67.pin1
  N13: Arduino.D3, Bauteil63.pin1
  N14: Arduino.D2, Bauteil66.pin1
  N15: Arduino.D1TX, Bauteil68.pin1
  N16: Arduino.D0RX, Bauteil69.pin1
  N17: Arduino.RST, Bauteil94.pin1
  N18: Arduino.3V3, Bauteil92.pin1
  N19: Arduino.+5V, Bauteil2.pin1, Bauteil3.pin1, Bauteil4.pin1, Bauteil5.pin1, Bauteil6.pin1, Bauteil7.pin1, Bauteil11.pin1, Bauteil15.pin1, Bauteil17.pin1, Bauteil113.pin1
  N20: Arduino.VIN, Bauteil9.pin1, Bauteil29.pin1, Bauteil45.pin1, Bauteil46.pin1, Bauteil47.pin1, Bauteil48.pin1, Bauteil49.pin1, Bauteil50.pin1, Bauteil51.pin1, Bauteil114.pin1
  N21: Arduino.A0, Bauteil115.pin1
  N22: Arduino.A1, Bauteil124.pin1
  N23: Arduino.A2, Bauteil120.pin1
  N24: Arduino.A3, Bauteil121.pin1
  N25: Arduino.A4, Bauteil122.pin1
  N26: Arduino.A5, Bauteil123.pin1
  N27: Arduino.reserved, Bauteil91.pin1
  N28: Arduino.IO_REF, Bauteil93.pin1
  N29: Arduino.SCL, Bauteil13.pin1
  N30: Arduino.SDA, Bauteil52.pin1

notes:
  2012 boxtec.ch
  A0 A1 A2 A3 A4 A5
  R 33V 5V |GND| VIN
  D0 D1 D2 D3 D4 D5 D6 D7
  D8 D9 10 11 12 13 GND
  SDA SCL
  GND
  | ------ 5V ------- |
  | ------ VIN ------ |
  |-GND-|
  Floweronly 0.1

custom parts:
  FlowerPad: FlowerPad Header
